# Fritzing sketch PCB (saved by Fritzing 1.0.1rc)
circuit board: 3.5cm x 3.52047cm

parts:
  5V = female pin header, 1 pin [form="♀ (female)"]
  J5 = female pin header, 5 pins [form="♀ (female)"]
  J6 = female pin header, 5 pins [form="♀ (female)"]
  J4 = female pin header, 1 pin [form="♀ (female)"]
  J8 = female pin header, 1 pin [form="♀ (female)"]
  J7 = female pin header, 4 pins [form="♀ (female)"]
  Left = female pin header, 4 pins [form="♀ (female)"]

nets:
  N1: 5V.pin1, J5.pin5
  N2: J5.pin1, Left.pin1
  N3: J5.pin2, Left.pin2
  N4: J5.pin3, Left.pin3
  N5: J5.pin4, Left.pin4
  N6: J6.pin1, J4.pin1, J8.pin1
  N7: J6.pin2, J7.pin4
  N8: J6.pin3, J7.pin3
  N9: J6.pin4, J7.pin2
  N10: J6.pin5, J7.pin1

notes:
  12
  14
  26
  27
  15
  2
  0
  4
  STEP
  DIR
  X
  Y
  Z
  A
  5V
  GND
  EN
